// Logisim project sqrt2.circ as structural Verilog: 47 circuits, main circuit sqrt
module main (
  input  ENABLE,
  input  [15:0] IO_DATA_IN,
  output NAN,
  output PINF,
  output NINF,
  output RESULT,
  output [15:0] IO_DATA_OUT
);

  wire CLK_out;

  Clock CLK (.out(CLK_out));
  sqrt sqrt_1 (
    .CLK(CLK_out), .ENABLE(ENABLE), .IO_DATA_IN(IO_DATA_IN), .NAN(NAN), .PINF(PINF), .NINF(NINF),
    .result(RESULT), .IO_DATA_OUT(IO_DATA_OUT));
endmodule

module sqrt (
  input  CLK,
  input  ENABLE,
  input  [15:0] IO_DATA_IN,
  output NAN,
  output PINF,
  output NINF,
  output result,
  output [15:0] IO_DATA_OUT
);

  wire and_1_out, and_3_out, and_4_out, and_5_out, bits_compare_8_1_scd_greater,
       bits_compare_8_2_scd_greater, d_trigger_1_nres, d_trigger_1_res, denormal_checker_denormal,
       exp_counter_carry_bit_out, minus_inf_checker_minus_inf, minus_zero_checker_minus_zero,
       nan_checker_nan, not_2_out, or_2_out, or_3_out, or_4_out, or_5_out, plus_inf_checker_plus_inf,
       plus_zero_checker_plus_zero, quiet_nan_checker_quiet_nan, transmission_1_p1, transmission_1_p4,
       undriven, undriven_2, undriven_3, undriven_4, undriven_5, undriven_6, undriven_7, undriven_8,
       undriven_9, undriven_10, undriven_11, undriven_12, undriven_13, undriven_14, undriven_15, undriven_16,
       undriven_17, undriven_18, undriven_19, undriven_20, undriven_21, undriven_22, undriven_23,
       undriven_24, undriven_25, undriven_26, undriven_27, undriven_28, undriven_29, undriven_30,
       undriven_31, undriven_32, undriven_33;
  wire [7:0] cyclee_counterr;
  wire [15:0] and_2_out, border_casess_result, cyclee_result, exp_counter_result,
       exp_getter_mant_shifter_exp_value, exp_getter_mant_shifter_mant_value, if_else_16_1_result,
       input_value_memory_value, mantissa_handler_memory_value, mnt1_out, normalization_exp_need_result,
       normalization_mant_need_result, normalizationn_output_exp, normalizationn_output_mant, or_1_out,
       result_exp_memory_value, transmission_1_p2, transmission_2_p2;
  wire [15:1] sign_hanldler_memory_value;
  wire [15:15] sign_hanldler_memory_value_2;

  // NoConnect on undriven
  // NoConnect on undriven_4
  // NoConnect on undriven_7
  // NoConnect on undriven_10
  // NoConnect on undriven_2
  // NoConnect on undriven_5
  // NoConnect on undriven_8
  // NoConnect on undriven_11
  // NoConnect on undriven_3
  // NoConnect on undriven_6
  // NoConnect on undriven_9
  // NoConnect on undriven_12
  and and_1 (and_1_out, d_trigger_1_nres, ENABLE);
  // NoConnect on undriven_13
  // NoConnect on undriven_16
  // NoConnect on undriven_19
  // NoConnect on undriven_21
  // NoConnect on undriven_23
  // NoConnect on undriven_25
  // NoConnect on undriven_27
  // NoConnect on undriven_29
  // NoConnect on undriven_14
  // NoConnect on undriven_17
  // NoConnect on undriven_20
  // NoConnect on undriven_22
  // NoConnect on undriven_24
  // NoConnect on undriven_26
  // NoConnect on undriven_28
  // NoConnect on undriven_15
  // NoConnect on undriven_18
  d_trigger d_trigger_1 (.ENABLE(ENABLE), .CLK(CLK), .D(1'b1), .nres(d_trigger_1_nres), .res(d_trigger_1_res));
  // NoConnect on d_trigger_1_res
  // NoConnect on undriven_30
  // NoConnect on undriven_31
  // NoConnect on undriven_32
  bits_memory_16 sign_hanldler (
    .ENABLE(ENABLE), .CLK(CLK), .input_value({{15{1'b0}}, input_value_memory_value[15]}),
    .memory_value({sign_hanldler_memory_value, sign_hanldler_memory_value_2[15]}));
  bits_memory_16 result_exp (
    .ENABLE(ENABLE), .CLK(CLK), .input_value({{11{1'b0}}, input_value_memory_value[14:10]}),
    .memory_value(result_exp_memory_value));
  bits_memory_16 mantissa_handler (
    .ENABLE(ENABLE), .CLK(CLK), .input_value({{6{1'b0}}, input_value_memory_value[9:0]}),
    .memory_value(mantissa_handler_memory_value));
  // NoConnect on undriven_33
  bits_memory_16 input_value (
    .ENABLE(ENABLE), .CLK(and_1_out), .input_value(transmission_1_p2), .memory_value(input_value_memory_value));
  is_denormal denormal_checker (.input_value(input_value_memory_value), .denormal(denormal_checker_denormal));
  assign and_2_out = result_exp_memory_value & {16{1'b0}};  // AND_Gate and_2, 16 bits wide
  assign mnt1_out = mantissa_handler_memory_value | 16'h400;  // OR_Gate mnt1, 16 bits wide
  normalization_full normalizationn (
    .input_exp(or_1_out), .input_mant(mantissa_handler_memory_value), .output_exp(normalizationn_output_exp),
    .output_mant(normalizationn_output_mant));
  assign or_1_out = and_2_out | 16'h12;  // OR_Gate or_1, 16 bits wide
  bits_summator_16 exp_counter (
    .first_value(result_exp_memory_value), .second_value(16'h11), .carry_bit_in(undriven_33),
    .result(exp_counter_result), .carry_bit_out(exp_counter_carry_bit_out));
  // NoConnect on exp_counter_carry_bit_out
  or or_2 (or_2_out, NAN, PINF, NINF, and_4_out, and_5_out, and_3_out);
  is_nann nan_checker (.input_value(input_value_memory_value), .nan(nan_checker_nan));
  is_plus_0 plus_zero_checker (.input_value(input_value_memory_value), .plus_zero(plus_zero_checker_plus_zero));
  is_quiet_nann quiet_nan_checker (.input_value(input_value_memory_value), .quiet_nan(quiet_nan_checker_quiet_nan));
  border_cases border_casess (
    .nan(NAN), .pinf(PINF), .ninf(NINF), .zero(and_4_out), .mzero(and_5_out), .qnan(and_3_out),
    .value(input_value_memory_value), .result(border_casess_result));
  // Transmission_Gate #(.width(16)) transmission_1: pin names not known; wires that end beside it: transmission_1_p1, transmission_1_p2, IO_DATA_IN, transmission_1_p4
  is_plus_inff plus_inf_checker (.input_value(input_value_memory_value), .plus_inf(plus_inf_checker_plus_inf));
  is_minus_0 minus_zero_checker (.input_value(input_value_memory_value), .minus_zero(minus_zero_checker_minus_zero));
  and and_3 (and_3_out, bits_compare_8_1_scd_greater, quiet_nan_checker_quiet_nan);
  if_else_16 normalization_exp_need (
    .condition(denormal_checker_denormal), .first(normalizationn_output_exp), .second(exp_counter_result),
    .result(normalization_exp_need_result));
  if_else_16 normalization_mant_need (
    .condition(denormal_checker_denormal), .first(normalizationn_output_mant), .second(mnt1_out),
    .result(normalization_mant_need_result));
  not not_1 (transmission_1_p4, transmission_1_p1);
  // Transmission_Gate #(.width(16)) transmission_2: pin names not known; wires that end beside it: transmission_1_p4, transmission_2_p2, IO_DATA_IN, transmission_1_p1
  // NoConnect on exp_getter_mant_shifter_mant_value[15]
  // NoConnect on exp_getter_mant_shifter_mant_value[14]
  if_else_16 resultt (
    .condition(or_2_out), .first(border_casess_result), .second(if_else_16_1_result),
    .result(transmission_2_p2));
  exp_value_getter exp_getter_mant_shifter (
    .input_exp(normalization_exp_need_result), .input_mant(normalization_mant_need_result),
    .mant_value(exp_getter_mant_shifter_mant_value), .exp_value(exp_getter_mant_shifter_exp_value));
  is_minus_inff minus_inf_checker (.input_value(input_value_memory_value), .minus_inf(minus_inf_checker_minus_inf));
  and and_4 (and_4_out, bits_compare_8_1_scd_greater, plus_zero_checker_plus_zero);
  and and_5 (and_5_out, bits_compare_8_1_scd_greater, minus_zero_checker_minus_zero);
  cycle cyclee (
    .CLK(CLK), .shifted_mant({exp_getter_mant_shifter_mant_value[13:0], {10{1'b0}}}), .remainder({24{1'b0}}),
    .mant({16{1'b0}}), .ENABLE(ENABLE), .result(cyclee_result), .counterr(cyclee_counterr));
  or or_3 (or_3_out, nan_checker_nan, and_3_out);
  or or_4 (or_4_out, and_4_out, and_3_out, and_5_out);
  bits_compare_8 bits_compare_8_1 (
    .first_input(8'h1), .second_input(cyclee_counterr), .scd_greater(bits_compare_8_1_scd_greater));
  // NoConnect on exp_getter_mant_shifter_exp_value[15]
  // NoConnect on exp_getter_mant_shifter_exp_value[14]
  // NoConnect on exp_getter_mant_shifter_exp_value[13]
  // NoConnect on exp_getter_mant_shifter_exp_value[12]
  // NoConnect on exp_getter_mant_shifter_exp_value[11]
  // NoConnect on exp_getter_mant_shifter_exp_value[10]
  // NoConnect on cyclee_result[15]
  // NoConnect on cyclee_result[14]
  // NoConnect on cyclee_result[13]
  // NoConnect on cyclee_result[12]
  // NoConnect on cyclee_result[11]
  // NoConnect on cyclee_result[10]
  // NoConnect on sign_hanldler_memory_value[15]
  // NoConnect on sign_hanldler_memory_value[14]
  // NoConnect on sign_hanldler_memory_value[13]
  // NoConnect on sign_hanldler_memory_value[12]
  // NoConnect on sign_hanldler_memory_value[11]
  // NoConnect on sign_hanldler_memory_value[10]
  // NoConnect on exp_getter_mant_shifter_exp_value[9]
  // NoConnect on exp_getter_mant_shifter_exp_value[8]
  // NoConnect on exp_getter_mant_shifter_exp_value[7]
  // NoConnect on exp_getter_mant_shifter_exp_value[6]
  // NoConnect on exp_getter_mant_shifter_exp_value[5]
  // NoConnect on sign_hanldler_memory_value[9]
  // NoConnect on sign_hanldler_memory_value[8]
  // NoConnect on sign_hanldler_memory_value[7]
  // NoConnect on sign_hanldler_memory_value[6]
  // NoConnect on sign_hanldler_memory_value[5]
  // NoConnect on sign_hanldler_memory_value[4]
  // NoConnect on sign_hanldler_memory_value[3]
  // NoConnect on sign_hanldler_memory_value[2]
  and and_6 (NAN, bits_compare_8_1_scd_greater, or_3_out);
  and and_7 (PINF, bits_compare_8_1_scd_greater, plus_inf_checker_plus_inf);
  and and_8 (NINF, bits_compare_8_1_scd_greater, minus_inf_checker_minus_inf);
  or or_5 (or_5_out, NAN, PINF, NINF);
  // NoConnect on sign_hanldler_memory_value[1]
  or or_6 (result, or_5_out, or_4_out, not_2_out);
  not not_2 (not_2_out, bits_compare_8_2_scd_greater);
  bits_compare_8 bits_compare_8_2 (
    .first_input(cyclee_counterr), .second_input(8'hc), .scd_greater(bits_compare_8_2_scd_greater));
  bits_compare_10 bits_compare_10_1 (
    .first_input({2'b00, cyclee_counterr}), .second_input(10'h2), .scd_greater(transmission_1_p1));
  if_else_16 if_else_16_1 (
    .condition(transmission_1_p1), .first({16{1'b0}}),
    .second({sign_hanldler_memory_value_2[15], exp_getter_mant_shifter_exp_value[4:0], cyclee_result[9:0]}),
    .result(if_else_16_1_result));

  assign IO_DATA_OUT = IO_DATA_IN;
endmodule

module cycle (
  input  CLK,
  input  [23:0] shifted_mant,
  input  [23:0] remainder,
  input  [15:0] mant,
  input  ENABLE,
  output [15:0] result,
  output [7:0] counterr
);

  wire and_1_out, bits_compare_10_1_scd_greater, bits_equality_8_1_equal, not_1_out, not_2_out, not_3_out;
  wire [15:0] bits_memory_16_1_memory_value, if_else_16_1_result, mantt_memory_value;
  wire [23:0] bits_memory_24_1_memory_value, bits_memory_24_2_memory_value, if_else_24_1_result,
       if_else_24_2_result, iteration_1_1_remainder_out, iteration_1_1_shifted_mant_out,
       remainderr_memory_value, shifted_mantt_memory_value;

  counter counter_1 (.CLK(CLK), .ENABLE(ENABLE), .counter_value(counterr));
  bits_compare_10 bits_compare_10_1 (
    .first_input({2'b00, counterr}), .second_input(10'hc), .scd_greater(bits_compare_10_1_scd_greater));
  and and_1 (and_1_out, bits_compare_10_1_scd_greater, CLK);
  bits_equality_8 bits_equality_8_1 (.first_input(counterr), .second_input(8'h1), .equal(bits_equality_8_1_equal));
  not not_1 (not_1_out, and_1_out);
  bits_memory_16 mantt (
    .ENABLE(ENABLE), .CLK(and_1_out), .input_value(if_else_16_1_result), .memory_value(mantt_memory_value));
  bits_memory_16 bits_memory_16_1 (
    .ENABLE(ENABLE), .CLK(not_1_out), .input_value(mantt_memory_value),
    .memory_value(bits_memory_16_1_memory_value));
  if_else_16 if_else_16_1 (
    .condition(bits_equality_8_1_equal), .first(mant), .second(result), .result(if_else_16_1_result));
  not not_2 (not_2_out, and_1_out);
  bits_memory_24 remainderr (
    .ENABLE(ENABLE), .CLK(and_1_out), .input_value(if_else_24_1_result),
    .memory_value(remainderr_memory_value));
  bits_memory_24 bits_memory_24_1 (
    .ENABLE(ENABLE), .CLK(not_2_out), .input_value(remainderr_memory_value),
    .memory_value(bits_memory_24_1_memory_value));
  if_else_24 if_else_24_1 (
    .condition(bits_equality_8_1_equal), .first(remainder), .second(iteration_1_1_remainder_out),
    .result(if_else_24_1_result));
  not not_3 (not_3_out, and_1_out);
  bits_memory_24 shifted_mantt (
    .ENABLE(ENABLE), .CLK(and_1_out), .input_value(if_else_24_2_result),
    .memory_value(shifted_mantt_memory_value));
  bits_memory_24 bits_memory_24_2 (
    .ENABLE(ENABLE), .CLK(not_3_out), .input_value(shifted_mantt_memory_value),
    .memory_value(bits_memory_24_2_memory_value));
  iteration_1 iteration_1_1 (
    .result_in(bits_memory_16_1_memory_value), .remainder_in(bits_memory_24_1_memory_value),
    .shifted_mant_in(bits_memory_24_2_memory_value), .result_out(result),
    .remainder_out(iteration_1_1_remainder_out), .shifted_mant_out(iteration_1_1_shifted_mant_out));
  if_else_24 if_else_24_2 (
    .condition(bits_equality_8_1_equal), .first(shifted_mant), .second(iteration_1_1_shifted_mant_out),
    .result(if_else_24_2_result));
endmodule

module border_cases (
  input  nan,
  input  pinf,
  input  ninf,
  input  zero,
  input  mzero,
  input  qnan,
  input  [15:0] value,
  output [15:0] result
);

  wire or_1_out, or_2_out;
  wire [15:0] if_else_16_1_result, if_else_16_2_result, if_else_16_3_result, if_else_16_4_result,
       if_else_16_5_result, if_else_16_6_result, if_else_16_7_result, if_else_16_8_result,
       if_else_16_9_result, if_else_16_10_result;

  if_else_16 if_else_16_1 (.condition(nan), .first(value), .second(16'h1), .result(if_else_16_1_result));
  if_else_16 if_else_16_2 (.condition(pinf), .first(16'h7c00), .second(16'h1), .result(if_else_16_2_result));
  if_else_16 if_else_16_3 (.condition(ninf), .first(16'hfe00), .second(16'h1), .result(if_else_16_3_result));
  if_else_16 if_else_16_4 (.condition(zero), .first({16{1'b0}}), .second(16'h1), .result(if_else_16_4_result));
  if_else_16 if_else_16_5 (.condition(mzero), .first(16'h8000), .second(16'h1), .result(if_else_16_5_result));
  if_else_16 if_else_16_6 (.condition(qnan), .first(16'hfe00), .second(16'h1), .result(if_else_16_6_result));
  or or_1 (or_1_out, nan, pinf);
  or or_2 (or_2_out, qnan, mzero);
  if_else_16 if_else_16_7 (
    .condition(nan), .first(if_else_16_1_result), .second(if_else_16_2_result), .result(if_else_16_7_result));
  if_else_16 if_else_16_8 (
    .condition(ninf), .first(if_else_16_3_result), .second(if_else_16_4_result), .result(if_else_16_8_result));
  if_else_16 if_else_16_9 (
    .condition(mzero), .first(if_else_16_5_result), .second(if_else_16_6_result), .result(if_else_16_9_result));
  if_else_16 if_else_16_10 (
    .condition(or_1_out), .first(if_else_16_7_result), .second(if_else_16_8_result),
    .result(if_else_16_10_result));
  if_else_16 if_else_16_11 (
    .condition(or_2_out), .first(if_else_16_9_result), .second(if_else_16_10_result), .result(result));
endmodule

module number_splitter (
  input  [15:0] input_value,
  output sign_value,
  output [4:0] exponent_value,
  output [9:0] mantissa_value
);


  assign exponent_value = input_value[14:10];
  assign mantissa_value = input_value[9:0];
  assign sign_value = input_value[15];
endmodule

module rs_trigger (
  input  ENABLE,
  input  set,
  input  CLK,
  input  reset,
  output nres,
  output res
);

  wire and_1_out, and_2_out, nor_1_out, nor_2_out, por_1_out;

  POR por_1 (.out(por_1_out));
  and and_1 (and_1_out, set, CLK);
  and and_2 (and_2_out, CLK, reset);
  nor nor_1 (nor_1_out, por_1_out, ENABLE);
  nor nor_2 (nor_2_out, and_1_out, res);
  nor nor_3 (res, nres, and_2_out);
  or or_1 (nres, nor_1_out, nor_2_out);
endmodule

module d_trigger (
  input  ENABLE,
  input  CLK,
  input  D,
  output nres,
  output res
);

  wire not_1_out;

  not not_1 (not_1_out, D);
  rs_trigger rs_trigger_1 (.ENABLE(ENABLE), .set(D), .CLK(CLK), .reset(not_1_out), .nres(nres), .res(res));
endmodule

module jk_trigger (
  input  kill,
  input  ENABLE,
  input  CLK,
  input  jump,
  output res,
  output nres
);

  wire and_1_out, and_2_out, not_1_out, rs_trigger_1_nres, rs_trigger_1_res;

  and and_1 (and_1_out, res, kill);
  and and_2 (and_2_out, jump, nres);
  rs_trigger rs_trigger_1 (
    .ENABLE(ENABLE), .set(and_2_out), .CLK(CLK), .reset(and_1_out), .nres(rs_trigger_1_nres),
    .res(rs_trigger_1_res));
  not not_1 (not_1_out, CLK);
  rs_trigger rs_trigger_2 (
    .ENABLE(ENABLE), .set(rs_trigger_1_res), .CLK(not_1_out), .reset(rs_trigger_1_nres), .nres(nres),
    .res(res));
endmodule

module counter (
  input  CLK,
  input  ENABLE,
  output [7:0] counter_value
);

  wire jk_trigger_1_nres, jk_trigger_2_nres, jk_trigger_3_nres, jk_trigger_4_nres, jk_trigger_5_nres,
       jk_trigger_6_nres, jk_trigger_7_nres, jk_trigger_8_nres;

  jk_trigger jk_trigger_1 (
    .kill(ENABLE), .ENABLE(ENABLE), .CLK(CLK), .jump(ENABLE), .res(counter_value[0]), .nres(jk_trigger_1_nres));
  // NoConnect on jk_trigger_1_nres
  jk_trigger jk_trigger_2 (
    .kill(ENABLE), .ENABLE(ENABLE), .CLK(counter_value[0]), .jump(ENABLE), .res(counter_value[1]),
    .nres(jk_trigger_2_nres));
  // NoConnect on jk_trigger_2_nres
  jk_trigger jk_trigger_3 (
    .kill(ENABLE), .ENABLE(ENABLE), .CLK(counter_value[1]), .jump(ENABLE), .res(counter_value[2]),
    .nres(jk_trigger_3_nres));
  // NoConnect on jk_trigger_3_nres
  jk_trigger jk_trigger_4 (
    .kill(ENABLE), .ENABLE(ENABLE), .CLK(counter_value[2]), .jump(ENABLE), .res(counter_value[3]),
    .nres(jk_trigger_4_nres));
  // NoConnect on jk_trigger_4_nres
  jk_trigger jk_trigger_5 (
    .kill(ENABLE), .ENABLE(ENABLE), .CLK(counter_value[3]), .jump(ENABLE), .res(counter_value[4]),
    .nres(jk_trigger_5_nres));
  // NoConnect on jk_trigger_5_nres
  jk_trigger jk_trigger_6 (
    .kill(ENABLE), .ENABLE(ENABLE), .CLK(counter_value[4]), .jump(ENABLE), .res(counter_value[5]),
    .nres(jk_trigger_6_nres));
  // NoConnect on jk_trigger_6_nres
  jk_trigger jk_trigger_7 (
    .kill(ENABLE), .ENABLE(ENABLE), .CLK(counter_value[5]), .jump(ENABLE), .res(counter_value[6]),
    .nres(jk_trigger_7_nres));
  // NoConnect on jk_trigger_7_nres
  jk_trigger jk_trigger_8 (
    .kill(ENABLE), .ENABLE(ENABLE), .CLK(counter_value[6]), .jump(ENABLE), .res(counter_value[7]),
    .nres(jk_trigger_8_nres));
  // NoConnect on jk_trigger_8_nres
endmodule

module is_plus_0 (
  input  [15:0] input_value,
  output plus_zero
);

  wire bits_equality_5_1_equal, bits_equality_10_1_equal, not_1_out, number_splitter_1_sign_value;
  wire [4:0] number_splitter_1_exponent_value;
  wire [9:0] number_splitter_1_mantissa_value;

  number_splitter number_splitter_1 (
    .input_value(input_value), .sign_value(number_splitter_1_sign_value),
    .exponent_value(number_splitter_1_exponent_value), .mantissa_value(number_splitter_1_mantissa_value));
  not not_1 (not_1_out, number_splitter_1_sign_value);
  bits_equality_5 bits_equality_5_1 (
    .first_input({5{1'b0}}), .second_input(number_splitter_1_exponent_value), .equal(bits_equality_5_1_equal));
  bits_equality_10 bits_equality_10_1 (
    .first_input({10{1'b0}}), .second_input(number_splitter_1_mantissa_value),
    .equal(bits_equality_10_1_equal));
  and and_1 (plus_zero, not_1_out, bits_equality_5_1_equal, bits_equality_10_1_equal);
endmodule

module is_minus_0 (
  input  [15:0] input_value,
  output minus_zero
);

  wire bits_equality_5_1_equal, bits_equality_10_1_equal, number_splitter_1_sign_value;
  wire [4:0] number_splitter_1_exponent_value;
  wire [9:0] number_splitter_1_mantissa_value;

  number_splitter number_splitter_1 (
    .input_value(input_value), .sign_value(number_splitter_1_sign_value),
    .exponent_value(number_splitter_1_exponent_value), .mantissa_value(number_splitter_1_mantissa_value));
  bits_equality_5 bits_equality_5_1 (
    .first_input({5{1'b0}}), .second_input(number_splitter_1_exponent_value), .equal(bits_equality_5_1_equal));
  bits_equality_10 bits_equality_10_1 (
    .first_input({10{1'b0}}), .second_input(number_splitter_1_mantissa_value),
    .equal(bits_equality_10_1_equal));
  and and_1 (minus_zero, number_splitter_1_sign_value, bits_equality_5_1_equal, bits_equality_10_1_equal);
endmodule

module is_nann (
  input  [15:0] input_value,
  output nan
);

  wire bits_compare_10_1_scd_greater, bits_equality_5_1_equal, number_splitter_1_sign_value, or_1_out;
  wire [4:0] number_splitter_1_exponent_value;
  wire [9:0] number_splitter_1_mantissa_value;

  number_splitter number_splitter_1 (
    .input_value(input_value), .sign_value(number_splitter_1_sign_value),
    .exponent_value(number_splitter_1_exponent_value), .mantissa_value(number_splitter_1_mantissa_value));
  or or_1 (or_1_out, number_splitter_1_sign_value, 1'b1);
  bits_equality_5 bits_equality_5_1 (
    .first_input({5{1'b1}}), .second_input(number_splitter_1_exponent_value), .equal(bits_equality_5_1_equal));
  bits_compare_10 bits_compare_10_1 (
    .first_input({10{1'b0}}), .second_input(number_splitter_1_mantissa_value),
    .scd_greater(bits_compare_10_1_scd_greater));
  and and_1 (nan, or_1_out, bits_equality_5_1_equal, bits_compare_10_1_scd_greater);
endmodule

module is_quiet_nann (
  input  [15:0] input_value,
  output quiet_nan
);

  wire is_minus_0_1_minus_zero, is_minus_inff_1_minus_inf, is_nann_1_nan, not_1_out, not_2_out, not_3_out,
       number_splitter_1_sign_value;
  wire [4:0] number_splitter_1_exponent_value;
  wire [9:0] number_splitter_1_mantissa_value;

  is_minus_0 is_minus_0_1 (.input_value(input_value), .minus_zero(is_minus_0_1_minus_zero));
  number_splitter number_splitter_1 (
    .input_value(input_value), .sign_value(number_splitter_1_sign_value),
    .exponent_value(number_splitter_1_exponent_value), .mantissa_value(number_splitter_1_mantissa_value));
  is_minus_inff is_minus_inff_1 (.input_value(input_value), .minus_inf(is_minus_inff_1_minus_inf));
  is_nann is_nann_1 (.input_value(input_value), .nan(is_nann_1_nan));
  not not_1 (not_1_out, is_minus_0_1_minus_zero);
  not not_2 (not_2_out, is_minus_inff_1_minus_inf);
  not not_3 (not_3_out, is_nann_1_nan);
  // NoConnect on number_splitter_1_exponent_value
  // NoConnect on number_splitter_1_mantissa_value
  and and_1 (quiet_nan, number_splitter_1_sign_value, not_1_out, not_2_out, not_3_out);
endmodule

module is_plus_inff (
  input  [15:0] input_value,
  output plus_inf
);

  wire bits_equality_5_1_equal, bits_equality_10_1_equal, not_1_out, number_splitter_1_sign_value;
  wire [4:0] number_splitter_1_exponent_value;
  wire [9:0] number_splitter_1_mantissa_value;

  number_splitter number_splitter_1 (
    .input_value(input_value), .sign_value(number_splitter_1_sign_value),
    .exponent_value(number_splitter_1_exponent_value), .mantissa_value(number_splitter_1_mantissa_value));
  not not_1 (not_1_out, number_splitter_1_sign_value);
  bits_equality_5 bits_equality_5_1 (
    .first_input({5{1'b1}}), .second_input(number_splitter_1_exponent_value), .equal(bits_equality_5_1_equal));
  bits_equality_10 bits_equality_10_1 (
    .first_input({10{1'b0}}), .second_input(number_splitter_1_mantissa_value),
    .equal(bits_equality_10_1_equal));
  and and_1 (plus_inf, not_1_out, bits_equality_5_1_equal, bits_equality_10_1_equal);
endmodule

module is_minus_inff (
  input  [15:0] input_value,
  output minus_inf
);

  wire bits_equality_5_1_equal, bits_equality_10_1_equal, number_splitter_1_sign_value;
  wire [4:0] number_splitter_1_exponent_value;
  wire [9:0] number_splitter_1_mantissa_value;

  number_splitter number_splitter_1 (
    .input_value(input_value), .sign_value(number_splitter_1_sign_value),
    .exponent_value(number_splitter_1_exponent_value), .mantissa_value(number_splitter_1_mantissa_value));
  bits_equality_5 bits_equality_5_1 (
    .first_input({5{1'b1}}), .second_input(number_splitter_1_exponent_value), .equal(bits_equality_5_1_equal));
  bits_equality_10 bits_equality_10_1 (
    .first_input({10{1'b0}}), .second_input(number_splitter_1_mantissa_value),
    .equal(bits_equality_10_1_equal));
  and and_1 (minus_inf, number_splitter_1_sign_value, bits_equality_5_1_equal, bits_equality_10_1_equal);
endmodule

module is_negative (
  input  [15:0] input_value,
  output negative
);

  wire bits_compare_5_1_scd_greater, bits_compare_5_2_scd_greater, bits_compare_10_1_scd_greater,
       number_splitter_1_sign_value;
  wire [4:0] number_splitter_1_exponent_value;
  wire [9:0] number_splitter_1_mantissa_value;

  number_splitter number_splitter_1 (
    .input_value(input_value), .sign_value(number_splitter_1_sign_value),
    .exponent_value(number_splitter_1_exponent_value), .mantissa_value(number_splitter_1_mantissa_value));
  bits_compare_5 bits_compare_5_1 (
    .first_input(number_splitter_1_exponent_value), .second_input({5{1'b1}}),
    .scd_greater(bits_compare_5_1_scd_greater));
  bits_compare_5 bits_compare_5_2 (
    .first_input({5{1'b0}}), .second_input(number_splitter_1_exponent_value),
    .scd_greater(bits_compare_5_2_scd_greater));
  bits_compare_10 bits_compare_10_1 (
    .first_input({10{1'b0}}), .second_input(number_splitter_1_mantissa_value),
    .scd_greater(bits_compare_10_1_scd_greater));
  and and_1 (negative, number_splitter_1_sign_value, bits_compare_5_1_scd_greater, bits_compare_5_2_scd_greater, bits_compare_10_1_scd_greater);
endmodule

module is_denormal (
  input  [15:0] input_value,
  output denormal
);

  wire bits_compare_10_1_scd_greater, bits_equality_5_1_equal, not_1_out, number_splitter_1_sign_value;
  wire [4:0] number_splitter_1_exponent_value;
  wire [9:0] number_splitter_1_mantissa_value;

  number_splitter number_splitter_1 (
    .input_value(input_value), .sign_value(number_splitter_1_sign_value),
    .exponent_value(number_splitter_1_exponent_value), .mantissa_value(number_splitter_1_mantissa_value));
  not not_1 (not_1_out, number_splitter_1_sign_value);
  bits_equality_5 bits_equality_5_1 (
    .first_input({5{1'b0}}), .second_input(number_splitter_1_exponent_value), .equal(bits_equality_5_1_equal));
  bits_compare_10 bits_compare_10_1 (
    .first_input({10{1'b0}}), .second_input(number_splitter_1_mantissa_value),
    .scd_greater(bits_compare_10_1_scd_greater));
  and and_1 (denormal, not_1_out, bits_equality_5_1_equal, bits_compare_10_1_scd_greater);
endmodule

module normalization_1 (
  input  [15:0] input_exp,
  input  [15:0] input_mant,
  output [15:0] output_exp,
  output [15:0] output_mant
);

  wire cond1_out;
  wire [15:0] bits_substractor_16_1_result;

  // NoConnect on input_mant[15]
  // NoConnect on 1'b0
  // NoConnect on 1'b0
  // NoConnect on 1'b0
  // NoConnect on 1'b0
  // NoConnect on 1'b0
  // NoConnect on 1'b0
  // NoConnect on 1'b0
  // NoConnect on 1'b0
  // NoConnect on 1'b0
  // NoConnect on 1'b0
  // NoConnect on 1'b0
  // NoConnect on 1'b0
  // NoConnect on 1'b0
  // NoConnect on 1'b0
  // NoConnect on 1'b0
  // NoConnect on input_mant[0]
  // NoConnect on input_mant[1]
  // NoConnect on input_mant[2]
  // NoConnect on input_mant[3]
  // NoConnect on input_mant[4]
  // NoConnect on input_mant[5]
  // NoConnect on input_mant[7]
  // NoConnect on input_mant[8]
  // NoConnect on input_mant[9]
  // NoConnect on input_mant[11]
  // NoConnect on input_mant[12]
  // NoConnect on input_mant[13]
  // NoConnect on input_mant[14]
  // NoConnect on input_mant[15]
  bits_substractor_16 bits_substractor_16_1 (
    .first_value(input_exp), .second_value(16'h1), .result(bits_substractor_16_1_result));
  and cond1 (cond1_out, 1'b1, input_mant[10]);
  if_else_16 exp_cond_1 (
    .condition(cond1_out), .first(input_exp), .second(bits_substractor_16_1_result), .result(output_exp));
  if_else_16 mant_cond_1 (
    .condition(cond1_out), .first(input_mant), .second({input_mant[14:0], 1'b0}), .result(output_mant));
endmodule

module normalization_full (
  input  [15:0] input_exp,
  input  [15:0] input_mant,
  output [15:0] output_exp,
  output [15:0] output_mant
);

  wire [15:0] normalization_1_1_output_exp, normalization_1_1_output_mant, normalization_1_2_output_exp,
       normalization_1_2_output_mant, normalization_1_3_output_exp, normalization_1_3_output_mant,
       normalization_1_4_output_exp, normalization_1_4_output_mant, normalization_1_5_output_exp,
       normalization_1_5_output_mant, normalization_1_6_output_exp, normalization_1_6_output_mant,
       normalization_1_7_output_exp, normalization_1_7_output_mant, normalization_1_8_output_exp,
       normalization_1_8_output_mant, normalization_1_9_output_exp, normalization_1_9_output_mant;

  normalization_1 normalization_1_1 (
    .input_exp(input_exp), .input_mant(input_mant), .output_exp(normalization_1_1_output_exp),
    .output_mant(normalization_1_1_output_mant));
  normalization_1 normalization_1_2 (
    .input_exp(normalization_1_1_output_exp), .input_mant(normalization_1_1_output_mant),
    .output_exp(normalization_1_2_output_exp), .output_mant(normalization_1_2_output_mant));
  normalization_1 normalization_1_3 (
    .input_exp(normalization_1_2_output_exp), .input_mant(normalization_1_2_output_mant),
    .output_exp(normalization_1_3_output_exp), .output_mant(normalization_1_3_output_mant));
  normalization_1 normalization_1_4 (
    .input_exp(normalization_1_3_output_exp), .input_mant(normalization_1_3_output_mant),
    .output_exp(normalization_1_4_output_exp), .output_mant(normalization_1_4_output_mant));
  normalization_1 normalization_1_5 (
    .input_exp(normalization_1_4_output_exp), .input_mant(normalization_1_4_output_mant),
    .output_exp(normalization_1_5_output_exp), .output_mant(normalization_1_5_output_mant));
  normalization_1 normalization_1_6 (
    .input_exp(normalization_1_5_output_exp), .input_mant(normalization_1_5_output_mant),
    .output_exp(normalization_1_6_output_exp), .output_mant(normalization_1_6_output_mant));
  normalization_1 normalization_1_7 (
    .input_exp(normalization_1_6_output_exp), .input_mant(normalization_1_6_output_mant),
    .output_exp(normalization_1_7_output_exp), .output_mant(normalization_1_7_output_mant));
  normalization_1 normalization_1_8 (
    .input_exp(normalization_1_7_output_exp), .input_mant(normalization_1_7_output_mant),
    .output_exp(normalization_1_8_output_exp), .output_mant(normalization_1_8_output_mant));
  normalization_1 normalization_1_9 (
    .input_exp(normalization_1_8_output_exp), .input_mant(normalization_1_8_output_mant),
    .output_exp(normalization_1_9_output_exp), .output_mant(normalization_1_9_output_mant));
  normalization_1 normalization_1_10 (
    .input_exp(normalization_1_9_output_exp), .input_mant(normalization_1_9_output_mant),
    .output_exp(output_exp), .output_mant(output_mant));
endmodule

module if_else_1 (
  input  condition,
  input  first,
  input  second,
  output result
);

  wire not_1_out, not_2_out;

  not not_1 (not_1_out, condition);
  not not_2 (not_2_out, condition);
  // Transmission_Gate transmission_1: pin names not known; wires that end beside it: first, not_1_out, condition, result
  // Transmission_Gate transmission_2: pin names not known; wires that end beside it: second, condition, not_2_out, result
endmodule

module if_else_16 (
  input  condition,
  input  [15:0] first,
  input  [15:0] second,
  output [15:0] result
);

  wire not_1_out, not_2_out;

  not not_1 (not_1_out, condition);
  not not_2 (not_2_out, condition);
  // Transmission_Gate #(.width(16)) transmission_1: pin names not known; wires that end beside it: first, not_1_out, condition, result
  // Transmission_Gate #(.width(16)) transmission_2: pin names not known; wires that end beside it: second, condition, not_2_out, result
endmodule

module if_else_24 (
  input  condition,
  input  [23:0] first,
  input  [23:0] second,
  output [23:0] result
);

  wire not_1_out, transmission_2_p3;

  not not_1 (not_1_out, condition);
  // Transmission_Gate #(.width(24)) transmission_1: pin names not known; wires that end beside it: first, not_1_out, condition, result
  // Transmission_Gate #(.width(24)) transmission_2: pin names not known; wires that end beside it: second, condition, transmission_2_p3, result
  not not_2 (transmission_2_p3, condition);
endmodule

module exp_value_getter (
  input  [15:0] input_exp,
  input  [15:0] input_mant,
  output [15:0] mant_value,
  output [15:0] exp_value
);

  wire and_1_out, bits_summator_24_1_carry_bit_out, undriven;
  wire [0:0] bits_substractor_24_1_result;
  wire [22:0] bits_substractor_24_1_result_2;
  wire [23:0] bits_substractor_24_2_result, if_else_24_2_result;
  wire [23:16] bits_summator_24_1_result, if_else_24_1_result;

  bits_substractor_24 bits_substractor_24_1 (
    .first_value(if_else_24_2_result), .second_value(24'h20),
    .result({bits_substractor_24_1_result_2, bits_substractor_24_1_result[0]}));
  // NoConnect on input_exp[1]
  // NoConnect on input_exp[2]
  // NoConnect on input_exp[3]
  // NoConnect on input_exp[4]
  // NoConnect on input_exp[5]
  // NoConnect on input_exp[6]
  // NoConnect on input_exp[7]
  // NoConnect on input_exp[8]
  // NoConnect on input_exp[9]
  // NoConnect on input_exp[10]
  // NoConnect on input_exp[11]
  // NoConnect on input_exp[12]
  // NoConnect on input_exp[13]
  // NoConnect on input_exp[14]
  // NoConnect on input_exp[15]
  // NoConnect on 1'b0
  // NoConnect on 1'b0
  // NoConnect on 1'b0
  // NoConnect on 1'b0
  // NoConnect on 1'b0
  // NoConnect on 1'b0
  // NoConnect on 1'b0
  // NoConnect on 1'b0
  // NoConnect on bits_substractor_24_1_result[0]
  and and_1 (and_1_out, input_exp[0], 1'b1);
  // NoConnect on undriven
  bits_substractor_24 bits_substractor_24_2 (
    .first_value({{8{1'b0}}, input_exp}), .second_value(24'h1), .result(bits_substractor_24_2_result));
  bits_summator_24 bits_summator_24_1 (
    .first_value({1'b0, bits_substractor_24_1_result_2}), .second_value(24'hf), .carry_bit_in(undriven),
    .result({bits_summator_24_1_result, exp_value}), .carry_bit_out(bits_summator_24_1_carry_bit_out));
  if_else_24 if_else_24_1 (
    .condition(and_1_out), .first({{7{1'b0}}, input_mant, 1'b0}), .second({{8{1'b0}}, input_mant}),
    .result({if_else_24_1_result, mant_value}));
  if_else_24 if_else_24_2 (
    .condition(and_1_out), .first(bits_substractor_24_2_result), .second({{8{1'b0}}, input_exp}),
    .result(if_else_24_2_result));
  // NoConnect on bits_summator_24_1_carry_bit_out
  // NoConnect on 1'b0
  // NoConnect on bits_summator_24_1_result[16]
  // NoConnect on bits_summator_24_1_result[17]
  // NoConnect on bits_summator_24_1_result[18]
  // NoConnect on bits_summator_24_1_result[19]
  // NoConnect on bits_summator_24_1_result[20]
  // NoConnect on bits_summator_24_1_result[21]
  // NoConnect on bits_summator_24_1_result[22]
  // NoConnect on bits_summator_24_1_result[23]
  // NoConnect on if_else_24_1_result[16]
  // NoConnect on if_else_24_1_result[17]
  // NoConnect on if_else_24_1_result[18]
  // NoConnect on if_else_24_1_result[19]
  // NoConnect on if_else_24_1_result[20]
  // NoConnect on if_else_24_1_result[21]
  // NoConnect on if_else_24_1_result[22]
  // NoConnect on if_else_24_1_result[23]
endmodule

module iteration_1 (
  input  [15:0] result_in,
  input  [23:0] remainder_in,
  input  [23:0] shifted_mant_in,
  output [15:0] result_out,
  output [23:0] remainder_out,
  output [23:0] shifted_mant_out
);

  wire bits_compare_24_1_scd_greater;
  wire [1:0] and_1_out, or_1_out;
  wire [23:0] bits_substractor_24_1_result;

  // NoConnect on remainder_in[22]
  // NoConnect on remainder_in[23]
  // NoConnect on shifted_mant_in[0]
  // NoConnect on shifted_mant_in[1]
  // NoConnect on shifted_mant_in[2]
  // NoConnect on shifted_mant_in[3]
  // NoConnect on shifted_mant_in[4]
  // NoConnect on shifted_mant_in[5]
  // NoConnect on shifted_mant_in[6]
  // NoConnect on shifted_mant_in[7]
  // NoConnect on shifted_mant_in[8]
  // NoConnect on shifted_mant_in[9]
  // NoConnect on shifted_mant_in[10]
  // NoConnect on shifted_mant_in[11]
  // NoConnect on shifted_mant_in[12]
  // NoConnect on shifted_mant_in[13]
  // NoConnect on shifted_mant_in[14]
  // NoConnect on shifted_mant_in[15]
  // NoConnect on shifted_mant_in[16]
  // NoConnect on shifted_mant_in[17]
  // NoConnect on shifted_mant_in[18]
  // NoConnect on shifted_mant_in[19]
  // NoConnect on shifted_mant_in[22]
  // NoConnect on shifted_mant_in[23]
  assign and_1_out = 2'b11 & shifted_mant_in[21:20];  // AND_Gate and_1, 2 bits wide
  // NoConnect on result_in[14]
  // NoConnect on result_in[15]
  assign or_1_out = 2'b00 | and_1_out;  // OR_Gate or_1, 2 bits wide
  // NoConnect on shifted_mant_in[22]
  // NoConnect on shifted_mant_in[23]
  // NoConnect on 1'b0
  bits_compare_24 bits_compare_24_1 (
    .first_input({remainder_in[21:0], or_1_out}), .second_input({{8{1'b0}}, result_in[13:0], 2'b01}),
    .scd_greater(bits_compare_24_1_scd_greater));
  // NoConnect on result_in[15]
  // NoConnect on result_in[15]
  bits_substractor_24 bits_substractor_24_1 (
    .first_value({remainder_in[21:0], or_1_out}), .second_value({{8{1'b0}}, result_in[13:0], 2'b01}),
    .result(bits_substractor_24_1_result));
  if_else_16 if_else_16_1 (
    .condition(bits_compare_24_1_scd_greater), .first({result_in[14:0], 1'b0}),
    .second({result_in[14:0], 1'b1}), .result(result_out));
  if_else_24 if_else_24_1 (
    .condition(bits_compare_24_1_scd_greater), .first({remainder_in[21:0], or_1_out}),
    .second(bits_substractor_24_1_result), .result(remainder_out));

  assign shifted_mant_out = {shifted_mant_in[21:0], 2'b00};

  // Notes on the sheet:
  //   remainder_in <<= 2
  //   shifted _mant_in >> 20 & 0x3
  //   temp = (result_in << 2)
  //   remaind_in | ((shifted_mant_in >> 20) & 0x3)
  //   temp | 1
  //   shifted_mant_in <<= 2
  //   remainder_in < temp
  //   result_in = result_in << 1
  //   result_in = (result_in << 1) | 1
  //   remaind_in -= temp
endmodule

module bits_equality_1 (
  input  first_value,
  input  second_value,
  output equality
);

  xnor xnor_1 (equality, first_value, second_value);
endmodule

module bits_equality_2 (
  input  [1:0] first_value,
  input  [1:0] second_value,
  output equality
);

  wire xnor_1_out, xnor_2_out;

  xnor xnor_1 (xnor_1_out, first_value[0], second_value[0]);
  xnor xnor_2 (xnor_2_out, first_value[1], second_value[1]);
  and and_1 (equality, xnor_1_out, xnor_2_out);
endmodule

module bits_equality_5 (
  input  [4:0] first_input,
  input  [4:0] second_input,
  output equal
);

  wire xnor_1_out, xnor_2_out, xnor_3_out, xnor_4_out, xnor_5_out;

  xnor xnor_1 (xnor_1_out, first_input[4], second_input[4]);
  xnor xnor_2 (xnor_2_out, first_input[3], second_input[3]);
  xnor xnor_3 (xnor_3_out, first_input[2], second_input[2]);
  xnor xnor_4 (xnor_4_out, first_input[1], second_input[1]);
  xnor xnor_5 (xnor_5_out, first_input[0], second_input[0]);
  and and_1 (equal, xnor_1_out, xnor_2_out, xnor_3_out, xnor_4_out, xnor_5_out);
endmodule

module bits_equality_8 (
  input  [7:0] first_input,
  input  [7:0] second_input,
  output equal
);

  wire bits_equality_2_1_equality, bits_equality_2_2_equality, bits_equality_2_3_equality,
       bits_equality_2_4_equality;

  bits_equality_2 bits_equality_2_1 (
    .first_value(first_input[1:0]), .second_value(second_input[1:0]), .equality(bits_equality_2_1_equality));
  bits_equality_2 bits_equality_2_2 (
    .first_value(first_input[3:2]), .second_value(second_input[3:2]), .equality(bits_equality_2_2_equality));
  bits_equality_2 bits_equality_2_3 (
    .first_value(first_input[5:4]), .second_value(second_input[5:4]), .equality(bits_equality_2_3_equality));
  bits_equality_2 bits_equality_2_4 (
    .first_value(first_input[7:6]), .second_value(second_input[7:6]), .equality(bits_equality_2_4_equality));
  and and_1 (equal, bits_equality_2_1_equality, bits_equality_2_2_equality, bits_equality_2_3_equality, bits_equality_2_4_equality);
endmodule

module bits_equality_10 (
  input  [9:0] first_input,
  input  [9:0] second_input,
  output equal
);

  wire bits_equality_5_1_equal, bits_equality_5_2_equal;

  bits_equality_5 bits_equality_5_1 (
    .first_input(first_input[4:0]), .second_input(second_input[4:0]), .equal(bits_equality_5_1_equal));
  bits_equality_5 bits_equality_5_2 (
    .first_input(first_input[9:5]), .second_input(second_input[9:5]), .equal(bits_equality_5_2_equal));
  and and_1 (equal, bits_equality_5_1_equal, bits_equality_5_2_equal);
endmodule

module bit_compare_1 (
  input  first_bit,
  input  second_bit,
  output scd_greater
);

  wire not_1_out;

  not not_1 (not_1_out, first_bit);
  and and_1 (scd_greater, not_1_out, second_bit);
endmodule

module bits_compare_2 (
  input  [1:0] first_input,
  input  [1:0] second_input,
  output scd_greater
);

  wire and_1_out, bit_compare_1_1_scd_greater, bit_compare_1_2_scd_greater, bits_equality_1_1_equality;

  bit_compare_1 bit_compare_1_1 (
    .first_bit(first_input[0]), .second_bit(second_input[0]), .scd_greater(bit_compare_1_1_scd_greater));
  bits_equality_1 bits_equality_1_1 (
    .first_value(first_input[1]), .second_value(second_input[1]), .equality(bits_equality_1_1_equality));
  bit_compare_1 bit_compare_1_2 (
    .first_bit(first_input[1]), .second_bit(second_input[1]), .scd_greater(bit_compare_1_2_scd_greater));
  and and_1 (and_1_out, bit_compare_1_1_scd_greater, bits_equality_1_1_equality);
  or or_1 (scd_greater, and_1_out, bit_compare_1_2_scd_greater);
endmodule

module bits_compare_4 (
  input  [3:0] first_input,
  input  [3:0] second_input,
  output scd_greater
);

  wire and_1_out, bits_compare_2_1_scd_greater, bits_compare_2_2_scd_greater, bits_equality_2_1_equality;

  bits_compare_2 bits_compare_2_1 (
    .first_input(first_input[1:0]), .second_input(second_input[1:0]),
    .scd_greater(bits_compare_2_1_scd_greater));
  bits_equality_2 bits_equality_2_1 (
    .first_value(first_input[3:2]), .second_value(second_input[3:2]), .equality(bits_equality_2_1_equality));
  bits_compare_2 bits_compare_2_2 (
    .first_input(first_input[3:2]), .second_input(second_input[3:2]),
    .scd_greater(bits_compare_2_2_scd_greater));
  and and_1 (and_1_out, bits_compare_2_1_scd_greater, bits_equality_2_1_equality);
  or or_1 (scd_greater, and_1_out, bits_compare_2_2_scd_greater);
endmodule

module bits_compare_5 (
  input  [4:0] first_input,
  input  [4:0] second_input,
  output scd_greater
);

  wire and_1_out, and_2_out, and_3_out, and_4_out, bit_compare_1_1_scd_greater, bit_compare_1_2_scd_greater,
       bit_compare_1_3_scd_greater, bit_compare_1_4_scd_greater, bit_compare_1_5_scd_greater,
       bits_equality_1_1_equality, bits_equality_1_2_equality, bits_equality_1_3_equality,
       bits_equality_1_4_equality, bits_equality_1_5_equality, bits_equality_1_6_equality,
       bits_equality_1_7_equality, bits_equality_1_8_equality, bits_equality_1_9_equality,
       bits_equality_1_10_equality;

  bit_compare_1 bit_compare_1_1 (
    .first_bit(first_input[0]), .second_bit(second_input[0]), .scd_greater(bit_compare_1_1_scd_greater));
  bits_equality_1 bits_equality_1_1 (
    .first_value(first_input[1]), .second_value(second_input[1]), .equality(bits_equality_1_1_equality));
  bits_equality_1 bits_equality_1_2 (
    .first_value(first_input[2]), .second_value(second_input[2]), .equality(bits_equality_1_2_equality));
  bits_equality_1 bits_equality_1_3 (
    .first_value(first_input[3]), .second_value(second_input[3]), .equality(bits_equality_1_3_equality));
  bits_equality_1 bits_equality_1_4 (
    .first_value(first_input[4]), .second_value(second_input[4]), .equality(bits_equality_1_4_equality));
  and and_1 (and_1_out, bit_compare_1_1_scd_greater, bits_equality_1_1_equality, bits_equality_1_2_equality, bits_equality_1_3_equality, bits_equality_1_4_equality);
  bit_compare_1 bit_compare_1_2 (
    .first_bit(first_input[1]), .second_bit(second_input[1]), .scd_greater(bit_compare_1_2_scd_greater));
  bits_equality_1 bits_equality_1_5 (
    .first_value(first_input[2]), .second_value(second_input[2]), .equality(bits_equality_1_5_equality));
  bits_equality_1 bits_equality_1_6 (
    .first_value(first_input[3]), .second_value(second_input[3]), .equality(bits_equality_1_6_equality));
  bits_equality_1 bits_equality_1_7 (
    .first_value(first_input[4]), .second_value(second_input[4]), .equality(bits_equality_1_7_equality));
  and and_2 (and_2_out, bit_compare_1_2_scd_greater, bits_equality_1_5_equality, bits_equality_1_6_equality, bits_equality_1_7_equality);
  bit_compare_1 bit_compare_1_3 (
    .first_bit(first_input[2]), .second_bit(second_input[2]), .scd_greater(bit_compare_1_3_scd_greater));
  bits_equality_1 bits_equality_1_8 (
    .first_value(first_input[3]), .second_value(second_input[3]), .equality(bits_equality_1_8_equality));
  bits_equality_1 bits_equality_1_9 (
    .first_value(first_input[4]), .second_value(second_input[4]), .equality(bits_equality_1_9_equality));
  and and_3 (and_3_out, bit_compare_1_3_scd_greater, bits_equality_1_8_equality, bits_equality_1_9_equality);
  bit_compare_1 bit_compare_1_4 (
    .first_bit(first_input[3]), .second_bit(second_input[3]), .scd_greater(bit_compare_1_4_scd_greater));
  bits_equality_1 bits_equality_1_10 (
    .first_value(first_input[4]), .second_value(second_input[4]), .equality(bits_equality_1_10_equality));
  and and_4 (and_4_out, bit_compare_1_4_scd_greater, bits_equality_1_10_equality);
  or or_1 (scd_greater, and_1_out, and_2_out, and_3_out, and_4_out, bit_compare_1_5_scd_greater);
  bit_compare_1 bit_compare_1_5 (
    .first_bit(first_input[4]), .second_bit(second_input[4]), .scd_greater(bit_compare_1_5_scd_greater));
endmodule

module bits_compare_8 (
  input  [7:0] first_input,
  input  [7:0] second_input,
  output scd_greater
);

  wire and_1_out, bits_compare_4_1_scd_greater, bits_compare_4_2_scd_greater, bits_equality_2_1_equality,
       bits_equality_2_2_equality;

  bits_compare_4 bits_compare_4_1 (
    .first_input(first_input[3:0]), .second_input(second_input[3:0]),
    .scd_greater(bits_compare_4_1_scd_greater));
  bits_equality_2 bits_equality_2_1 (
    .first_value(first_input[5:4]), .second_value(second_input[5:4]), .equality(bits_equality_2_1_equality));
  bits_equality_2 bits_equality_2_2 (
    .first_value(first_input[7:6]), .second_value(second_input[7:6]), .equality(bits_equality_2_2_equality));
  bits_compare_4 bits_compare_4_2 (
    .first_input(first_input[7:4]), .second_input(second_input[7:4]),
    .scd_greater(bits_compare_4_2_scd_greater));
  and and_1 (and_1_out, bits_compare_4_1_scd_greater, bits_equality_2_1_equality, bits_equality_2_2_equality);
  or or_1 (scd_greater, and_1_out, bits_compare_4_2_scd_greater);
endmodule

module bits_compare_10 (
  input  [9:0] first_input,
  input  [9:0] second_input,
  output scd_greater
);

  wire and_1_out, bits_compare_5_1_scd_greater, bits_compare_5_2_scd_greater, bits_equality_5_1_equal;

  bits_compare_5 bits_compare_5_1 (
    .first_input(first_input[4:0]), .second_input(second_input[4:0]),
    .scd_greater(bits_compare_5_1_scd_greater));
  bits_equality_5 bits_equality_5_1 (
    .first_input(first_input[9:5]), .second_input(second_input[9:5]), .equal(bits_equality_5_1_equal));
  bits_compare_5 bits_compare_5_2 (
    .first_input(first_input[9:5]), .second_input(second_input[9:5]),
    .scd_greater(bits_compare_5_2_scd_greater));
  and and_1 (and_1_out, bits_compare_5_1_scd_greater, bits_equality_5_1_equal);
  or or_1 (scd_greater, and_1_out, bits_compare_5_2_scd_greater);
endmodule

module bits_compare_24 (
  input  [23:0] first_input,
  input  [23:0] second_input,
  output scd_greater
);

  wire and_1_out, and_2_out, bits_compare_4_1_scd_greater, bits_compare_10_1_scd_greater,
       bits_compare_10_2_scd_greater, bits_equality_10_1_equal, bits_equality_10_2_equal,
       bits_equality_10_3_equal;

  bits_compare_4 bits_compare_4_1 (
    .first_input(first_input[3:0]), .second_input(second_input[3:0]),
    .scd_greater(bits_compare_4_1_scd_greater));
  bits_equality_10 bits_equality_10_1 (
    .first_input(first_input[13:4]), .second_input(second_input[13:4]), .equal(bits_equality_10_1_equal));
  bits_equality_10 bits_equality_10_2 (
    .first_input(first_input[23:14]), .second_input(second_input[23:14]), .equal(bits_equality_10_2_equal));
  bits_compare_10 bits_compare_10_1 (
    .first_input(first_input[13:4]), .second_input(second_input[13:4]),
    .scd_greater(bits_compare_10_1_scd_greater));
  bits_equality_10 bits_equality_10_3 (
    .first_input(first_input[23:14]), .second_input(second_input[23:14]), .equal(bits_equality_10_3_equal));
  bits_compare_10 bits_compare_10_2 (
    .first_input(first_input[23:14]), .second_input(second_input[23:14]),
    .scd_greater(bits_compare_10_2_scd_greater));
  and and_1 (and_1_out, bits_compare_4_1_scd_greater, bits_equality_10_1_equal, bits_equality_10_2_equal);
  and and_2 (and_2_out, bits_compare_10_1_scd_greater, bits_equality_10_3_equal);
  or or_1 (scd_greater, and_1_out, and_2_out, bits_compare_10_2_scd_greater);
endmodule

module bits_summator_1 (
  input  first_value,
  input  second_value,
  input  carry_bit_in,
  output result,
  output carry_bit_out
);

  wire and_1_out, and_2_out, xor_1_out;

  xor xor_1 (xor_1_out, first_value, second_value);
  and and_1 (and_1_out, xor_1_out, carry_bit_in);
  and and_2 (and_2_out, first_value, second_value);
  xor xor_2 (result, xor_1_out, carry_bit_in);
  or or_1 (carry_bit_out, and_1_out, and_2_out);
endmodule

module bits_summator_2 (
  input  [1:0] first_value,
  input  [1:0] second_value,
  input  carry_bit_in,
  output [1:0] result,
  output carry_bit_out
);

  wire bits_summator_1_1_carry_bit_out;

  bits_summator_1 bits_summator_1_1 (
    .first_value(first_value[0]), .second_value(second_value[0]), .carry_bit_in(carry_bit_in),
    .result(result[0]), .carry_bit_out(bits_summator_1_1_carry_bit_out));
  bits_summator_1 bits_summator_1_2 (
    .first_value(first_value[1]), .second_value(second_value[1]),
    .carry_bit_in(bits_summator_1_1_carry_bit_out), .result(result[1]), .carry_bit_out(carry_bit_out));
endmodule

module bits_summator_4 (
  input  [3:0] first_value,
  input  [3:0] second_value,
  input  carry_bit_in,
  output [3:0] result,
  output carry_bit_out
);

  wire bits_summator_2_1_carry_bit_out;

  bits_summator_2 bits_summator_2_1 (
    .first_value(first_value[1:0]), .second_value(second_value[1:0]), .carry_bit_in(carry_bit_in),
    .result(result[1:0]), .carry_bit_out(bits_summator_2_1_carry_bit_out));
  bits_summator_2 bits_summator_2_2 (
    .first_value(first_value[3:2]), .second_value(second_value[3:2]),
    .carry_bit_in(bits_summator_2_1_carry_bit_out), .result(result[3:2]), .carry_bit_out(carry_bit_out));
endmodule

module bits_summator_8 (
  input  [7:0] first_value,
  input  [7:0] second_value,
  input  carry_bit_in,
  output [7:0] result,
  output carry_bit_out
);

  wire bits_summator_4_1_carry_bit_out;

  bits_summator_4 bits_summator_4_1 (
    .first_value(first_value[3:0]), .second_value(second_value[3:0]), .carry_bit_in(carry_bit_in),
    .result(result[3:0]), .carry_bit_out(bits_summator_4_1_carry_bit_out));
  bits_summator_4 bits_summator_4_2 (
    .first_value(first_value[7:4]), .second_value(second_value[7:4]),
    .carry_bit_in(bits_summator_4_1_carry_bit_out), .result(result[7:4]), .carry_bit_out(carry_bit_out));
endmodule

module bits_summator_16 (
  input  [15:0] first_value,
  input  [15:0] second_value,
  input  carry_bit_in,
  output [15:0] result,
  output carry_bit_out
);

  wire bits_summator_8_1_carry_bit_out;

  bits_summator_8 bits_summator_8_1 (
    .first_value(first_value[7:0]), .second_value(second_value[7:0]), .carry_bit_in(carry_bit_in),
    .result(result[7:0]), .carry_bit_out(bits_summator_8_1_carry_bit_out));
  bits_summator_8 bits_summator_8_2 (
    .first_value(first_value[15:8]), .second_value(second_value[15:8]),
    .carry_bit_in(bits_summator_8_1_carry_bit_out), .result(result[15:8]), .carry_bit_out(carry_bit_out));
endmodule

module bits_summator_24 (
  input  [23:0] first_value,
  input  [23:0] second_value,
  input  carry_bit_in,
  output [23:0] result,
  output carry_bit_out
);

  wire bits_summator_16_1_carry_bit_out;

  bits_summator_16 bits_summator_16_1 (
    .first_value(first_value[15:0]), .second_value(second_value[15:0]), .carry_bit_in(carry_bit_in),
    .result(result[15:0]), .carry_bit_out(bits_summator_16_1_carry_bit_out));
  bits_summator_8 bits_summator_8_1 (
    .first_value(first_value[23:16]), .second_value(second_value[23:16]),
    .carry_bit_in(bits_summator_16_1_carry_bit_out), .result(result[23:16]), .carry_bit_out(carry_bit_out));
endmodule

module bits_substractor_16 (
  input  [15:0] first_value,
  input  [15:0] second_value,
  output [15:0] result
);

  wire bits_summator_16_1_carry_bit_out, bits_summator_16_2_carry_bit_out;
  wire [15:0] bits_summator_16_1_result, not_1_out;

  assign not_1_out = ~second_value;  // NOT_Gate not_1, 16 bits wide
  bits_summator_16 bits_summator_16_1 (
    .first_value(16'h1), .second_value(not_1_out), .carry_bit_in(1'b0), .result(bits_summator_16_1_result),
    .carry_bit_out(bits_summator_16_1_carry_bit_out));
  // NoConnect on bits_summator_16_1_carry_bit_out
  bits_summator_16 bits_summator_16_2 (
    .first_value(first_value), .second_value(bits_summator_16_1_result), .carry_bit_in(1'b0),
    .result(result), .carry_bit_out(bits_summator_16_2_carry_bit_out));
  // NoConnect on bits_summator_16_2_carry_bit_out
endmodule

module bits_substractor_24 (
  input  [23:0] first_value,
  input  [23:0] second_value,
  output [23:0] result
);

  wire bits_summator_24_1_carry_bit_out, bits_summator_24_2_carry_bit_out;
  wire [23:0] bits_summator_24_1_result, not_1_out;

  assign not_1_out = ~second_value;  // NOT_Gate not_1, 24 bits wide
  bits_summator_24 bits_summator_24_1 (
    .first_value(24'h1), .second_value(not_1_out), .carry_bit_in(1'b0), .result(bits_summator_24_1_result),
    .carry_bit_out(bits_summator_24_1_carry_bit_out));
  // NoConnect on bits_summator_24_1_carry_bit_out
  bits_summator_24 bits_summator_24_2 (
    .first_value(first_value), .second_value(bits_summator_24_1_result), .carry_bit_in(1'b0),
    .result(result), .carry_bit_out(bits_summator_24_2_carry_bit_out));
  // NoConnect on bits_summator_24_2_carry_bit_out
endmodule

module bits_memory_8 (
  input  ENABLE,
  input  CLK,
  input  [7:0] input_value,
  output [7:0] memory_value
);

  wire d_trigger_1_nres, d_trigger_2_nres, d_trigger_3_nres, d_trigger_4_nres, d_trigger_5_nres,
       d_trigger_6_nres, d_trigger_7_nres, d_trigger_8_nres;

  // NoConnect on d_trigger_1_nres
  d_trigger d_trigger_1 (
    .ENABLE(ENABLE), .CLK(CLK), .D(input_value[0]), .nres(d_trigger_1_nres), .res(memory_value[0]));
  // NoConnect on d_trigger_2_nres
  d_trigger d_trigger_2 (
    .ENABLE(ENABLE), .CLK(CLK), .D(input_value[1]), .nres(d_trigger_2_nres), .res(memory_value[1]));
  // NoConnect on d_trigger_3_nres
  d_trigger d_trigger_3 (
    .ENABLE(ENABLE), .CLK(CLK), .D(input_value[2]), .nres(d_trigger_3_nres), .res(memory_value[2]));
  // NoConnect on d_trigger_4_nres
  d_trigger d_trigger_4 (
    .ENABLE(ENABLE), .CLK(CLK), .D(input_value[3]), .nres(d_trigger_4_nres), .res(memory_value[3]));
  // NoConnect on d_trigger_5_nres
  d_trigger d_trigger_5 (
    .ENABLE(ENABLE), .CLK(CLK), .D(input_value[4]), .nres(d_trigger_5_nres), .res(memory_value[4]));
  // NoConnect on d_trigger_6_nres
  d_trigger d_trigger_6 (
    .ENABLE(ENABLE), .CLK(CLK), .D(input_value[5]), .nres(d_trigger_6_nres), .res(memory_value[5]));
  // NoConnect on d_trigger_7_nres
  d_trigger d_trigger_7 (
    .ENABLE(ENABLE), .CLK(CLK), .D(input_value[6]), .nres(d_trigger_7_nres), .res(memory_value[6]));
  // NoConnect on d_trigger_8_nres
  d_trigger d_trigger_8 (
    .ENABLE(ENABLE), .CLK(CLK), .D(input_value[7]), .nres(d_trigger_8_nres), .res(memory_value[7]));
endmodule

module bits_memory_16 (
  input  ENABLE,
  input  CLK,
  input  [15:0] input_value,
  output [15:0] memory_value
);

  bits_memory_8 bits_memory_8_1 (
    .ENABLE(ENABLE), .CLK(CLK), .input_value(input_value[7:0]), .memory_value(memory_value[7:0]));
  bits_memory_8 bits_memory_8_2 (
    .ENABLE(ENABLE), .CLK(CLK), .input_value(input_value[15:8]), .memory_value(memory_value[15:8]));
endmodule

module bits_memory_24 (
  input  ENABLE,
  input  CLK,
  input  [23:0] input_value,
  output [23:0] memory_value
);

  bits_memory_8 bits_memory_8_1 (
    .ENABLE(ENABLE), .CLK(CLK), .input_value(input_value[7:0]), .memory_value(memory_value[7:0]));
  bits_memory_8 bits_memory_8_2 (
    .ENABLE(ENABLE), .CLK(CLK), .input_value(input_value[15:8]), .memory_value(memory_value[15:8]));
  bits_memory_8 bits_memory_8_3 (
    .ENABLE(ENABLE), .CLK(CLK), .input_value(input_value[23:16]), .memory_value(memory_value[23:16]));
endmodule
